// Logisim project 1715881_Abdullah_lab.circ as structural Verilog: 1 circuit, main circuit main
module main (
  input  a,
  input  b,
  input  c,
  input  d,
  input  e,
  input  in_6,
  input  _1,
  input  _2,
  input  _3,
  input  _4,
  input  _5,
  output out_12,
  output out_13
);

  wire and_1_out, not_1_out, xnor_1_out, xnor_2_out, xnor_3_out, xnor_4_out, xnor_5_out;

  xnor xnor_1 (xnor_1_out, a, _1);
  xnor xnor_2 (xnor_2_out, b, _2);
  xnor xnor_3 (xnor_3_out, c, _3);
  xnor xnor_4 (xnor_4_out, d, _4);
  xnor xnor_5 (xnor_5_out, e, _5);
  and and_1 (and_1_out, xnor_1_out, xnor_2_out, xnor_3_out, xnor_4_out, xnor_5_out);
  not not_1 (not_1_out, and_1_out);
  and and_2 (out_12, and_1_out, in_6);
  LED led_1 (.in(out_12));
  and and_3 (out_13, not_1_out, in_6);
  LED led_2 (.in(out_13));
endmodule
